# Fritzing sketch Spark-Doorbell (saved by Fritzing 0.7.12b)

parts:
  LED1 = LED - 3mm [color="Red (633nm)" package="3 mm [THT]"]
  R2 = Resistor [tolerance=±5% resistance=150 package=THT]
  Part2 = JeeNode wireless microcontroller
  T2 = DS18B20 Temperature Sensor [part_number=DS18B20 package="TO92 [THT]"]
  R5 = Resistor [tolerance=±5% resistance=100k package=THT]
  S2 = Pushbutton [package="[THT]"]
  Power_plug1 = Power plug [part_number=3.6V]

nets:
  GND: LED1.cathode, Part2.GND, T2.GND, S2.Pin_2, Power_plug1.GND
  N1: LED1.anode, R2.Pin_1
  N2: R2.Pin_0, Part2.SCK
  N3: Part2.PWX, Power_plug1.VCC
  N4: Part2.VCC, T2.+Vdd, R5.Pin_0
  N5: Part2.INT2, R5.Pin_1, S2.Pin_3, S2.Pin_4
  N6: Part2.B0, T2.DQ

notes:
  3.6V (3x1.2V)

custom parts:
  DS18B20 Temperature Sensor: A DS18B20 temperature sensor
